# Fritzing sketch VL53L0X array each with its own Arduino (saved by Fritzing 0.9.3b)
breadboards: 1

parts:
  sensor = Adafruit VL53L0X Time of Flight Distance Sensor [part_number="Adafruit #3317"]
  host_(at_computer) = Arduino Nano (Rev3.0)
  sensor_module = Arduino Nano (Rev3.0)
  signal_diode = Rectifier Diode [part_number=1N4001 package="300 mil [THT]"]

nets:
  VIN: sensor.VIN, sensor_module.3V3
  GND: sensor.GND, host_(at_computer).GND, sensor_module.GND
  N1: sensor.SCL, sensor_module.A5
  N2: sensor.SDA, sensor_module.A4
  trigger_signal: host_(at_computer).D2, sensor_module.D2
  UART bus: host_(at_computer).D5, signal_diode.anode
  5V: host_(at_computer).5V, sensor_module.5V
  N3: sensor_module.D6, signal_diode.cathode

notes:
  To give sensor arduinos unique addresses, ground the following pins:
  Arduino # | pin(s) to ground
  0 | none
  1 | A1
  2 | A2
  3 | A1 and A2
  4 | A3
  Configuration used in practice had 5 Arduinos wired identically to the power and communication lines like so:

custom parts:
  Adafruit VL53L0X Time of Flight Distance Sensor: The VL53L0X is a Time of Flight distance sensor like no other you've used! The sensor contains a very tiny invisible laser source, and a matching sensor. The VL53L0X can detect the "time of flight", or how long the light has taken to bounce back to the sensor. Since it uses a very narrow light source, it is good for determining distance of only the surface directly in front of it. Unlike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
